# Fritzing sketch pride necklace (saved by Fritzing 0.9.3b)

parts:
  Part1 = GEMMA v2
  Part2 = 16 NeoPixel Ring [part_number=1463]
  R1 = Resistor [tolerance=±5% resistance=10k package="1206 [SMD]"]
  S1 = Pushbutton [package=THT]

nets:
  N1: Part1.3.3V, S1.leg0
  N2: Part1.B0, S1.leg1
  N3: Part1.B1, Part2.IN
  N4: Part1.B2, R1.Pin_1
  GND: Part1.GND, Part2.GND
  N5: Part1.Vout, Part2.VDD

custom parts:
  GEMMA v2: Love FLORA but want a bite-sized version? Look no further, GEMMA is a tiny wearable platform board with a lot of might in a 1" diameter package. Powered by a Attiny85 and programmable with an Arduino IDE over USB, you'll be able to realize any wearable project! We wanted to design a microcontroller board that was small enough to fit into any project, and low cost enough to use without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
  16 NeoPixel Ring: 16 ultra bright smart LED NeoPixels are arranged in a circle with 1.75" (44.5mm) outer diameter. The rings are 'chainable' - connect the output pin of one to the input pin of another. Use only one microcontroller pin to control as many as you can chain together! Each LED is addressable as the driver chip is inside the LED. Each one has ~18mA constant current drive so the color will be very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
